# Fritzing sketch hebi (saved by Fritzing 0.7.11b)
perfboards: 1

parts:
  U1 = atmega168 [package=dip]
  S1 = Pushbutton [package="[THT]"]
  XTAL1 = Crystal [frequency="16 Mhz" package=THT]
  S2 = Pushbutton [package="[THT]"]
  J2 = female pin header, 2 pins [form="♀ (female)"]
  J2_2 = male pin header, 4 pins [form="♂ (male)"]
  J1 = male pin header, 4 pins [form="♂ (male)"]
  J3 = male pin header, 3 pins [form="♂ (male)"]
  J4 = female pin header, 4 pins [form="♀ (female)"]
  J5 = male pin header, 3 pins [form="♂ (male)"]
  J6 = male pin header, 3 pins [form="♂ (male)"]
  J7 = male pin header, 3 pins [form="♂ (male)"]
  J8 = female pin header, 2 pins [form="♀ (female)"]
  J10 = male pin header, 4 pins [form="♂ (male)"]
  J9 = male pin header, 4 pins [form="♂ (male)"]
  J11 = longpad pin header, 3 pins [form="long pad"]
  J12 = longpad pin header, 3 pins [form="long pad"]
  J13 = longpad pin header, 3 pins [form="long pad"]

nets:
  N1: U1.RESET, J1.pin1, J12.pin1, J12.pin3
  N2: U1.D0_(RX), J1.pin2
  N3: U1.D1_(TX), J1.pin3
  N4: U1.D2, J2.pin1
  N5: U1.D3_(PWM), J2.pin2
  N6: U1.GND#7, U1.AVCC, J5.pin2, J6.pin2, J7.pin2
  N7: U1.XLAT1, XTAL1.pin_0
  N8: U1.XLAT2, XTAL1.pin_1
  N9: U1.D5_(PWM), J8.pin1
  N10: U1.D6_(PWM), J8.pin2
  N11: U1.D7, J10.pin2
  N12: U1.D8, J7.pin3
  N13: U1.D9_(PWM), J6.pin3
  N14: U1.D10_(PWM), J5.pin3
  N15: U1.D11_(PWM), J10.pin3
  N16: U1.D12, J9.pin4
  N17: U1.GND#21, J5.pin1, J7.pin1
  N18: U1.A0, J3.pin3
  N19: U1.A1, J3.pin2, J4.pin3
  N20: U1.A2, J3.pin1, J4.pin2
  N21: U1.A3, J4.pin1
  N22: U1.A4, J2_2.pin3
  N23: U1.A5, J2_2.pin2
  N24: S1.Pin_1, S1.Pin_2
  N25: S1.Pin_3, S1.Pin_4, J2_2.pin1, J1.pin4
  N26: S2.Pin_1, S2.Pin_2
  N27: S2.Pin_3, S2.Pin_4
  N28: J11.pin1, J11.pin3
  N29: J13.pin1, J13.pin3
